// Logisim project 8 bit ALU.circ as structural Verilog
module ALU (
  input  [7:0] OPERAND_2,
  input  [7:0] OPERAND_1,
  input  CIN,
  input  CIN_2,
  input  [3:0] OPCODE,
  input  OE,
  output COUT,
  output COUT_2,
  output [7:0] OUTPUT,
  output out_10,
  output GT,
  output EQ,
  output LT
);

  wire [2:0] bit_extender_1_out, bit_extender_2_out;
  wire [7:0] adder_1_out, adder_2_out, and_1_out, multiplexer_1_out, not_1_out, or_1_out, shifter_1_out,
       shifter_2_out, subtractor_1_out;

  Bit_Extender #(.out_width(3)) bit_extender_1 (.in(OPERAND_2), .out(bit_extender_1_out));
  Bit_Extender #(.out_width(3)) bit_extender_2 (.in(OPERAND_2), .out(bit_extender_2_out));
  Adder adder_1 (.a(OPERAND_1), .b(OPERAND_2), .out(adder_1_out), .cin(CIN), .cout(COUT));
  Adder adder_2 (.a(OPERAND_1), .b(8'h1), .out(adder_2_out), .cin(CIN_2), .cout(COUT_2));
  Subtractor subtractor_1 (.a(OPERAND_1), .b(8'h1), .out(subtractor_1_out), .bout(out_10));  // open: bin
  Comparator comparator_1 (.a(OPERAND_1), .b(OPERAND_2), .gt(GT), .eq(EQ), .lt(LT));
  assign not_1_out = ~OPERAND_1;  // NOT_Gate not_1, 8 bits wide
  assign and_1_out = OPERAND_1 & OPERAND_2;  // AND_Gate and_1, 8 bits wide
  assign or_1_out = OPERAND_1 | OPERAND_2;  // OR_Gate or_1, 8 bits wide
  Shifter #(.shift("lr")) shifter_1 (.in(OPERAND_1), .\dist (bit_extender_1_out), .out(shifter_1_out));
  Shifter shifter_2 (.in(OPERAND_1), .\dist (bit_extender_2_out), .out(shifter_2_out));
  Multiplexer #(.select(4), .width(8)) multiplexer_1 (
    .in0(adder_1_out), .in1(adder_2_out), .in2(subtractor_1_out), .in3(not_1_out), .in4(and_1_out),
    .in5(or_1_out), .in6(shifter_1_out), .in7(shifter_2_out), .out(multiplexer_1_out), .sel(OPCODE), .en(OE));  // open: in8, in9, in10, in11, in12, in13, in14, in15
  assign OUTPUT = multiplexer_1_out;  // Buffer buffer_1, 8 bits wide
endmodule

module _8_BIT_REGISTER (
  input  in_1,
  input  LOAD,
  input  D0,
  input  D1,
  input  D2,
  input  D3,
  input  D4,
  input  O5,
  input  D5,
  input  D6,
  input  D7,
  output out_12,
  output out_13,
  output out_14,
  output out_15,
  output out_16,
  output out_17,
  output out_18,
  output out_19
);

  wire and_1_out, and_2_out, and_3_out, and_4_out, and_5_out, and_6_out, and_7_out, and_8_out, and_9_out,
       and_10_out, and_11_out, and_12_out, and_13_out, and_14_out, and_15_out, and_16_out, not_1_out,
       not_2_out, not_3_out, not_4_out, not_5_out, not_6_out, not_7_out, not_8_out, or_1_out, or_2_out,
       or_3_out, or_4_out, or_5_out, or_6_out, or_7_out;

  not not_1 (not_1_out, LOAD);
  not not_2 (not_2_out, LOAD);
  not not_3 (not_3_out, LOAD);
  not not_4 (not_4_out, LOAD);
  not not_5 (not_5_out, LOAD);
  not not_6 (not_6_out, LOAD);
  not not_7 (not_7_out, LOAD);
  not not_8 (not_8_out, LOAD);
  and and_1 (and_1_out, out_12, not_1_out);
  and and_2 (and_2_out, LOAD, D0);
  and and_3 (and_3_out, out_13, not_2_out);
  and and_4 (and_4_out, LOAD, D1);
  and and_5 (and_5_out, out_14, not_3_out);
  and and_6 (and_6_out, LOAD, D2);
  and and_7 (and_7_out, out_15, not_4_out);
  and and_8 (and_8_out, LOAD, D3);
  and and_9 (and_9_out, out_16, not_5_out);
  and and_10 (and_10_out, LOAD, D4);
  and and_11 (and_11_out, O5, not_6_out);
  and and_12 (and_12_out, LOAD, D5);
  and and_13 (and_13_out, out_18, not_7_out);
  and and_14 (and_14_out, LOAD, D6);
  and and_15 (and_15_out, out_19, not_8_out);
  and and_16 (and_16_out, LOAD, D7);
  or or_1 (or_1_out, and_1_out, and_2_out);
  or or_2 (or_2_out, and_3_out, and_4_out);
  or or_3 (or_3_out, and_5_out, and_6_out);
  or or_4 (or_4_out, and_7_out, and_8_out);
  or or_5 (or_5_out, and_9_out, and_10_out);
  or or_6 (or_6_out, and_11_out, and_12_out);
  or or_7 (or_7_out, and_13_out, and_14_out);
  // OR_Gate or_8 has open pins: in0=and_15_out, in1=and_16_out, out=open
  D_Flip_Flop d_ff_1 (.clk(in_1), .D(or_2_out), .Q(out_13));  // open: Qn, preset, en, reset
  D_Flip_Flop d_ff_2 (.clk(in_1), .D(or_3_out), .Q(out_14));  // open: Qn, preset, en, reset
  D_Flip_Flop d_ff_3 (.clk(in_1), .D(or_4_out), .Q(out_15));  // open: Qn, preset, en, reset
  D_Flip_Flop d_ff_4 (.clk(in_1), .D(or_5_out), .Q(out_16));  // open: Qn, preset, en, reset
  D_Flip_Flop d_ff_5 (.clk(in_1), .D(or_6_out), .Q(O5));  // open: Qn, preset, en, reset
  D_Flip_Flop d_ff_6 (.clk(in_1), .D(or_7_out), .Q(out_18));  // open: Qn, preset, en, reset
  D_Flip_Flop d_ff_7 (.clk(in_1), .Q(out_19));  // open: D, Qn, preset, en, reset
  D_Flip_Flop d_ff_8 (.clk(in_1), .D(or_1_out), .Q(out_12));  // open: Qn, preset, en, reset
endmodule
