// Logisim project 8_bit_cpu_latest.circ as structural Verilog: 18 circuits, main circuit main
module main (
  input  CLR,
  input  in_2,
  input  in_3,
  input  in_4,
  input  in_5,
  output [3:0] HIGH,
  output [3:0] LOW,
  output out_8,
  output out_9,
  output out_10,
  output out_11,
  output [7:0] out_12
);

  wire ADD, CLK_out, controlled_buffer_1_out, Cp, EA, Ep, EU, nCE, nEI, nL0, nLA, nLB, nLI, nLM, not_1_out,
       not_2_out, not_3_out, not_4_out, not_5_out, not_6_out, not_7_out, SU;
  wire [3:0] register_4_bit_1_y0, register_8_bit_1_y0, register_8_bit_1_y4;
  wire [7:0] register_8_bit_2_y0, register_8_bit_3_y0;

  not not_1 (not_1_out, nLM);
  not not_2 (not_2_out, nCE);
  Controller controller_1 (
    .I7_I6_I5_I4(register_8_bit_1_y4), .Cp(Cp), .Ep(Ep), .nLM(nLM), .nCE(nCE), .nLi(nLI), .nEI(nEI),
    .nLA(nLA), .EA(EA), .SU(SU), .nL0(nL0), .EU(EU), .nLB(nLB), .ADD(ADD), .CLK(controlled_buffer_1_out),
    .CLR(CLR));
  not not_3 (not_3_out, in_2);
  Program_Counter program_counter_1 (
    .C3(LOW[3]), .C2(LOW[2]), .C1(LOW[1]), .C0(LOW[0]), .COUNT(Cp), .CLR(CLR), .CLK(controlled_buffer_1_out),
    .ENABLE(Ep));
  Register_4_bit register_4_bit_1 (
    .X3(LOW[3]), .X2(LOW[2]), .X1(LOW[1]), .X0(LOW[0]), .Y3(register_4_bit_1_y0[3]),
    .Y2(register_4_bit_1_y0[2]), .Y1(register_4_bit_1_y0[1]), .Y0(register_4_bit_1_y0[0]), .LOAD(not_1_out),
    .CLK(controlled_buffer_1_out), .CLR(CLR), .ENABLE(1'b1));
  RAM #(.addrWidth(4)) ram_1 (.addr(register_4_bit_1_y0), .data({HIGH, LOW}), .ld(not_2_out));  // open: sel, clk, clr
  Register_8_bit register_8_bit_1 (
    .X7(HIGH[3]), .X6(HIGH[2]), .X5(HIGH[1]), .X4(HIGH[0]), .X3(LOW[3]), .X2(LOW[2]), .X1(LOW[1]),
    .X0(LOW[0]), .Y7(register_8_bit_1_y4[3]), .Y6(register_8_bit_1_y4[2]), .Y5(register_8_bit_1_y4[1]),
    .Y4(register_8_bit_1_y4[0]), .Y3(register_8_bit_1_y0[3]), .Y2(register_8_bit_1_y0[2]),
    .Y1(register_8_bit_1_y0[1]), .Y0(register_8_bit_1_y0[0]), .LOAD(not_4_out),
    .CLK(controlled_buffer_1_out), .CLR(CLR), .ENABLE(1'b1));
  Clock CLK (.out(CLK_out));
  assign controlled_buffer_1_out = not_3_out ? CLK_out : 1'bz;  // Controlled_Buffer controlled_buffer_1
  not not_4 (not_4_out, nLI);
  assign LOW = not_5_out ? register_8_bit_1_y0 : 4'bz;  // Controlled_Buffer controlled_buffer_2
  not not_5 (not_5_out, nEI);
  not not_6 (not_6_out, nLA);
  Register_8_bit register_8_bit_2 (
    .X7(HIGH[3]), .X6(HIGH[2]), .X5(HIGH[1]), .X4(HIGH[0]), .X3(LOW[3]), .X2(LOW[2]), .X1(LOW[1]),
    .X0(LOW[0]), .Y7(register_8_bit_2_y0[7]), .Y6(register_8_bit_2_y0[6]), .Y5(register_8_bit_2_y0[5]),
    .Y4(register_8_bit_2_y0[4]), .Y3(register_8_bit_2_y0[3]), .Y2(register_8_bit_2_y0[2]),
    .Y1(register_8_bit_2_y0[1]), .Y0(register_8_bit_2_y0[0]), .LOAD(not_6_out),
    .CLK(controlled_buffer_1_out), .CLR(CLR), .ENABLE(1'b1));
  assign {HIGH, LOW} = EA ? register_8_bit_2_y0 : 8'bz;  // Controlled_Buffer controlled_buffer_3
  assign {HIGH, LOW} = EU ? out_12 : 8'bz;  // Controlled_Buffer controlled_buffer_4
  not not_7 (not_7_out, nLB);
  Register_8_bit register_8_bit_3 (
    .X7(HIGH[3]), .X6(HIGH[2]), .X5(HIGH[1]), .X4(HIGH[0]), .X3(LOW[3]), .X2(LOW[2]), .X1(LOW[1]),
    .X0(LOW[0]), .Y7(register_8_bit_3_y0[7]), .Y6(register_8_bit_3_y0[6]), .Y5(register_8_bit_3_y0[5]),
    .Y4(register_8_bit_3_y0[4]), .Y3(register_8_bit_3_y0[3]), .Y2(register_8_bit_3_y0[2]),
    .Y1(register_8_bit_3_y0[1]), .Y0(register_8_bit_3_y0[0]), .LOAD(not_7_out),
    .CLK(controlled_buffer_1_out), .CLR(CLR), .ENABLE(1'b1));
  ALU alu_1 (
    .SU(in_5), .ADD(ADD), .AND(in_4), .RS(in_3), .AC(register_8_bit_2_y0), .RB(register_8_bit_3_y0),
    .COUT(out_11), .OUTPUT(out_12), .EQ(out_10), .GT(out_9), .LT(out_8));  // open: INC, DEC, NOT, OR, FILL, LS, FILL_2

  // Notes on the sheet:
  //   IR
  //   ENABLE
  //   A
  //   B
endmodule

module FA (
  input  X,
  input  Y,
  input  Z,
  output S,
  output C
);

  wire AND_1_out, AND_2_out, XOR_1_out;

  xor XOR_1 (XOR_1_out, X, Y);
  and AND_1 (AND_1_out, X, Y);
  xor XOR_2 (S, XOR_1_out, Z);
  and AND_2 (AND_2_out, Z, XOR_1_out);
  or OR (C, AND_2_out, AND_1_out);
endmodule

// MAR
module Register_4_bit (
  input  X3,
  input  X2,
  input  X1,
  input  X0,
  input  LOAD,
  input  CLK,
  input  CLR,
  input  ENABLE,
  output Y3,
  output Y2,
  output Y1,
  output Y0
);

  wire and_1_out, and_2_out, and_3_out, and_4_out, and_5_out, and_6_out, and_7_out, and_8_out, d_ff_1_q,
       d_ff_2_q, d_ff_3_q, d_ff_4_q, not_1_out, or_1_out, or_2_out, or_3_out, or_4_out;

  and and_1 (and_1_out, d_ff_1_q, not_1_out);
  and and_2 (and_2_out, X3, LOAD);
  or or_1 (or_1_out, and_1_out, and_2_out);
  D_Flip_Flop d_ff_1 (.clk(CLK), .D(or_1_out), .Q(d_ff_1_q), .reset(CLR));  // open: Qn, preset, en
  assign Y3 = ENABLE ? d_ff_1_q : 1'bz;  // Controlled_Buffer controlled_buffer_1
  and and_3 (and_3_out, d_ff_2_q, not_1_out);
  or or_2 (or_2_out, and_3_out, and_4_out);
  and and_4 (and_4_out, X2, LOAD);
  D_Flip_Flop d_ff_2 (.clk(CLK), .D(or_2_out), .Q(d_ff_2_q), .reset(CLR));  // open: Qn, preset, en
  assign Y2 = ENABLE ? d_ff_2_q : 1'bz;  // Controlled_Buffer controlled_buffer_2
  and and_5 (and_5_out, d_ff_3_q, not_1_out);
  or or_3 (or_3_out, and_5_out, and_6_out);
  and and_6 (and_6_out, X1, LOAD);
  D_Flip_Flop d_ff_3 (.clk(CLK), .D(or_3_out), .Q(d_ff_3_q), .reset(CLR));  // open: Qn, preset, en
  and and_7 (and_7_out, d_ff_4_q, not_1_out);
  assign Y1 = ENABLE ? d_ff_3_q : 1'bz;  // Controlled_Buffer controlled_buffer_3
  not not_1 (not_1_out, LOAD);
  and and_8 (and_8_out, X0, LOAD);
  or or_4 (or_4_out, and_7_out, and_8_out);
  D_Flip_Flop d_ff_4 (.clk(CLK), .D(or_4_out), .Q(d_ff_4_q), .reset(CLR));  // open: Qn, preset, en
  assign Y0 = ENABLE ? d_ff_4_q : 1'bz;  // Controlled_Buffer controlled_buffer_4
endmodule

module Register_8_bit (
  input  X3,
  input  X2,
  input  X1,
  input  X0,
  input  X7,
  input  X6,
  input  X5,
  input  X4,
  input  LOAD,
  input  CLK,
  input  CLR,
  input  ENABLE,
  output Y3,
  output Y2,
  output Y1,
  output Y0,
  output Y5,
  output Y4,
  output Y7,
  output Y6
);

  wire and_1_out, and_2_out, and_3_out, and_4_out, and_5_out, and_6_out, and_7_out, and_8_out, and_9_out,
       and_10_out, and_11_out, and_12_out, and_13_out, and_14_out, and_15_out, and_16_out, d_ff_1_q,
       d_ff_2_q, d_ff_3_q, d_ff_4_q, d_ff_5_q, d_ff_6_q, d_ff_7_q, d_ff_8_q, not_1_out, or_1_out, or_2_out,
       or_3_out, or_4_out, or_5_out, or_6_out, or_7_out, or_8_out;

  and and_1 (and_1_out, X7, LOAD);
  and and_2 (and_2_out, d_ff_1_q, not_1_out);
  or or_1 (or_1_out, and_2_out, and_1_out);
  D_Flip_Flop d_ff_1 (.clk(CLK), .D(or_1_out), .Q(d_ff_1_q), .reset(CLR));  // open: Qn, preset, en
  assign Y7 = ENABLE ? d_ff_1_q : 1'bz;  // Controlled_Buffer controlled_buffer_1
  and and_3 (and_3_out, d_ff_2_q, not_1_out);
  or or_2 (or_2_out, and_3_out, and_4_out);
  and and_4 (and_4_out, X6, LOAD);
  D_Flip_Flop d_ff_2 (.clk(CLK), .D(or_2_out), .Q(d_ff_2_q), .reset(CLR));  // open: Qn, preset, en
  assign Y6 = ENABLE ? d_ff_2_q : 1'bz;  // Controlled_Buffer controlled_buffer_2
  and and_5 (and_5_out, d_ff_3_q, not_1_out);
  or or_3 (or_3_out, and_5_out, and_6_out);
  and and_6 (and_6_out, X5, LOAD);
  D_Flip_Flop d_ff_3 (.clk(CLK), .D(or_3_out), .Q(d_ff_3_q), .reset(CLR));  // open: Qn, preset, en
  and and_7 (and_7_out, d_ff_4_q, not_1_out);
  assign Y5 = ENABLE ? d_ff_3_q : 1'bz;  // Controlled_Buffer controlled_buffer_3
  and and_8 (and_8_out, X4, LOAD);
  or or_4 (or_4_out, and_7_out, and_8_out);
  D_Flip_Flop d_ff_4 (.clk(CLK), .D(or_4_out), .Q(d_ff_4_q), .reset(CLR));  // open: Qn, preset, en
  assign Y4 = ENABLE ? d_ff_4_q : 1'bz;  // Controlled_Buffer controlled_buffer_4
  and and_9 (and_9_out, d_ff_5_q, not_1_out);
  or or_5 (or_5_out, and_9_out, and_10_out);
  and and_10 (and_10_out, X3, LOAD);
  D_Flip_Flop d_ff_5 (.clk(CLK), .D(or_5_out), .Q(d_ff_5_q), .reset(CLR));  // open: Qn, preset, en
  assign Y3 = ENABLE ? d_ff_5_q : 1'bz;  // Controlled_Buffer controlled_buffer_5
  and and_11 (and_11_out, d_ff_6_q, not_1_out);
  or or_6 (or_6_out, and_11_out, and_12_out);
  and and_12 (and_12_out, X2, LOAD);
  D_Flip_Flop d_ff_6 (.clk(CLK), .D(or_6_out), .Q(d_ff_6_q), .reset(CLR));  // open: Qn, preset, en
  and and_13 (and_13_out, d_ff_7_q, not_1_out);
  assign Y2 = ENABLE ? d_ff_6_q : 1'bz;  // Controlled_Buffer controlled_buffer_6
  and and_14 (and_14_out, X1, LOAD);
  or or_7 (or_7_out, and_13_out, and_14_out);
  D_Flip_Flop d_ff_7 (.clk(CLK), .D(or_7_out), .Q(d_ff_7_q), .reset(CLR));  // open: Qn, preset, en
  and and_15 (and_15_out, d_ff_8_q, not_1_out);
  assign Y1 = ENABLE ? d_ff_7_q : 1'bz;  // Controlled_Buffer controlled_buffer_7
  not not_1 (not_1_out, LOAD);
  and and_16 (and_16_out, X0, LOAD);
  or or_8 (or_8_out, and_15_out, and_16_out);
  D_Flip_Flop d_ff_8 (.clk(CLK), .D(or_8_out), .Q(d_ff_8_q), .reset(CLR));  // open: Qn, preset, en
  assign Y0 = ENABLE ? d_ff_8_q : 1'bz;  // Controlled_Buffer controlled_buffer_8

  // Notes on the sheet:
  //   Roll: 1607048
endmodule

module ALU (
  input  [7:0] AC,
  input  [7:0] RB,
  input  SU,
  input  ADD,
  input  INC,
  input  DEC,
  input  NOT,
  input  AND,
  input  OR,
  input  FILL,
  input  LS,
  input  FILL_2,
  input  RS,
  output COUT,
  output [7:0] OUTPUT,
  output EQ,
  output GT,
  output LT
);

  wire [7:0] adder_1_s, controlled_buffer_2_out, decrement_1_s, increment_1_s, left_shift_1_out,
       logic_bitwise_and_1_out, logic_bitwise_not_1_out, logic_bitwise_or_1_out, right_shift_1_out;

  ADDER adder_1 (.X(AC), .Y(RB), .SU(SU), .S(adder_1_s), .Cout(COUT));
  INCREMENT increment_1 (.X(AC), .Y(RB), .S(increment_1_s));  // open: Cout
  DECREMENT decrement_1 (.X(AC), .Y(RB), .S(decrement_1_s));  // open: Cout
  LOGIC_BITWISE_NOT logic_bitwise_not_1 (.IN(AC), .OUT(logic_bitwise_not_1_out));
  LOGIC_BITWISE_AND logic_bitwise_and_1 (.X(RB), .Y(AC), .OUT(logic_bitwise_and_1_out));
  LOGIC_BITWISE_OR logic_bitwise_or_1 (.X(AC), .Y(RB), .OUT(logic_bitwise_or_1_out));
  LEFT_SHIFT left_shift_1 (.FILL(FILL), .IN(AC), .OUT(left_shift_1_out));
  RIGHT_SHIFT right_shift_1 (.IN(AC), .FILL(FILL_2), .OUT(right_shift_1_out));
  COMPARE compare_1 (.ACC(AC), .REG_B(RB), .EQ(EQ), .GT(GT), .LT(LT));
  assign OUTPUT = ADD ? adder_1_s : 8'bz;  // Controlled_Buffer controlled_buffer_1
  assign controlled_buffer_2_out = INC ? increment_1_s : 8'bz;  // Controlled_Buffer controlled_buffer_2
  assign controlled_buffer_2_out = DEC ? decrement_1_s : 8'bz;  // Controlled_Buffer controlled_buffer_3
  assign controlled_buffer_2_out = NOT ? logic_bitwise_not_1_out : 8'bz;  // Controlled_Buffer controlled_buffer_4
  assign controlled_buffer_2_out = AND ? logic_bitwise_and_1_out : 8'bz;  // Controlled_Buffer controlled_buffer_5
  assign controlled_buffer_2_out = OR ? logic_bitwise_or_1_out : 8'bz;  // Controlled_Buffer controlled_buffer_6
  assign controlled_buffer_2_out = LS ? left_shift_1_out : 8'bz;  // Controlled_Buffer controlled_buffer_7
  assign controlled_buffer_2_out = RS ? right_shift_1_out : 8'bz;  // Controlled_Buffer controlled_buffer_8

  // Notes on the sheet:
  //   ADD/ SUB
  //   INCREMENT
  //   DECREMENT
  //   BIWISE NOT
  //   BITWISE AND
  //   BITWISE OR
  //   REGISTER LEFT SHIFT
  //   REGISTER RIGHT SHFT
  //   COMPARISON
endmodule

// PC
module Program_Counter (
  input  COUNT,
  input  CLR,
  input  CLK,
  input  ENABLE,
  output C3,
  output C2,
  output C1,
  output C0
);

  wire AND1_out, AND2_out, AND3_out, j_k_ff_1_q, j_k_ff_2_q, j_k_ff_3_q, j_k_ff_4_q;

  and AND3 (AND3_out, COUNT, AND2_out, j_k_ff_2_q);
  J_K_Flip_Flop j_k_ff_1 (.J(AND3_out), .clk(CLK), .K(AND3_out), .Q(j_k_ff_1_q), .reset(CLR));  // open: Qn, preset, en
  assign C3 = ENABLE ? j_k_ff_1_q : 1'bz;  // Controlled_Buffer controlled_buffer_1
  and AND2 (AND2_out, COUNT, AND1_out, j_k_ff_3_q);
  J_K_Flip_Flop j_k_ff_2 (.J(AND2_out), .clk(CLK), .K(AND2_out), .Q(j_k_ff_2_q), .reset(CLR));  // open: Qn, preset, en
  assign C2 = ENABLE ? j_k_ff_2_q : 1'bz;  // Controlled_Buffer controlled_buffer_2
  and AND1 (AND1_out, COUNT, j_k_ff_4_q);
  J_K_Flip_Flop j_k_ff_3 (.J(AND1_out), .clk(CLK), .K(AND1_out), .Q(j_k_ff_3_q), .reset(CLR));  // open: Qn, preset, en
  assign C1 = ENABLE ? j_k_ff_3_q : 1'bz;  // Controlled_Buffer controlled_buffer_3
  J_K_Flip_Flop j_k_ff_4 (.J(COUNT), .clk(CLK), .K(COUNT), .Q(j_k_ff_4_q), .reset(CLR));  // open: Qn, preset, en
  assign C0 = ENABLE ? j_k_ff_4_q : 1'bz;  // Controlled_Buffer controlled_buffer_4
endmodule

// R Counter
module Ring_Counter (
  input  CLK,
  input  CLR,
  output T6,
  output T5,
  output T4,
  output T3,
  output T2,
  output T1
);

  wire j_k_ff_1_qn, j_k_ff_2_qn, j_k_ff_3_qn, j_k_ff_4_qn, j_k_ff_5_qn, j_k_ff_6_q;

  J_K_Flip_Flop j_k_ff_1 (
    .J(T5), .clk(CLK), .K(j_k_ff_2_qn), .Q(T6), .Qn(j_k_ff_1_qn), .reset(CLR));  // open: preset, en
  J_K_Flip_Flop j_k_ff_2 (
    .J(T4), .clk(CLK), .K(j_k_ff_3_qn), .Q(T5), .Qn(j_k_ff_2_qn), .reset(CLR));  // open: preset, en
  J_K_Flip_Flop j_k_ff_3 (
    .J(T3), .clk(CLK), .K(j_k_ff_4_qn), .Q(T4), .Qn(j_k_ff_3_qn), .reset(CLR));  // open: preset, en
  J_K_Flip_Flop j_k_ff_4 (
    .J(T2), .clk(CLK), .K(j_k_ff_5_qn), .Q(T3), .Qn(j_k_ff_4_qn), .reset(CLR));  // open: preset, en
  J_K_Flip_Flop j_k_ff_5 (
    .J(T1), .clk(CLK), .K(j_k_ff_6_q), .Q(T2), .Qn(j_k_ff_5_qn), .reset(CLR));  // open: preset, en
  J_K_Flip_Flop j_k_ff_6 (
    .J(j_k_ff_1_qn), .clk(CLK), .K(T6), .Q(j_k_ff_6_q), .Qn(T1), .reset(CLR));  // open: preset, en
endmodule

module Decoder (
  input  I7,
  input  I6,
  input  I5,
  input  I4,
  output LDA,
  output ADD___SUB,
  output LBA,
  output LSR,
  output LDB
);

  wire and_1_out, and_2_out, and_3_out, and_4_out, and_5_out, not_1_out, not_2_out, not_3_out, not_4_out;

  not not_1 (not_1_out, I7);
  not not_2 (not_2_out, I6);
  not not_3 (not_3_out, I5);
  not not_4 (not_4_out, I4);
  and and_1 (and_1_out, I7, not_2_out, not_3_out, I4);
  and and_2 (and_2_out, not_1_out, not_2_out, not_3_out, not_4_out);
  and and_3 (and_3_out, not_1_out, I6, not_3_out, I4);
  and and_4 (and_4_out, not_1_out, I6, I5, I4);
  and and_5 (and_5_out, I7, not_2_out, I5, not_4_out);
  buf buffer_1 (LDA, and_1_out);
  buf buffer_2 (ADD___SUB, and_2_out);
  buf buffer_3 (LBA, and_3_out);
  buf buffer_4 (LSR, and_4_out);
  buf buffer_5 (LDB, and_5_out);
endmodule

// CONTROLLER
module Controller (
  input  CLK,
  input  CLR,
  input  [3:0] I7_I6_I5_I4,
  output Cp,
  output Ep,
  output nLM,
  output nCE,
  output nLi,
  output nEI,
  output nLA,
  output EA,
  output SU,
  output nL0,
  output EU,
  output nLB,
  output ADD
);

  wire and_1_out, and_2_out, and_3_out, and_4_out, and_5_out, and_6_out, decoder_1_add___sub, decoder_1_lba,
       decoder_1_lda, decoder_1_ldb, decoder_1_lsr, or_1_out, or_2_out, or_3_out, or_4_out, or_6_out,
       ring_counter_1_t3, ring_counter_1_t4, ring_counter_1_t5, ring_counter_1_t6;

  Decoder decoder_1 (
    .I7(I7_I6_I5_I4[3]), .I6(I7_I6_I5_I4[2]), .I5(I7_I6_I5_I4[1]), .I4(I7_I6_I5_I4[0]), .LDA(decoder_1_lda),
    .ADD___SUB(decoder_1_add___sub), .LBA(decoder_1_lba), .LSR(decoder_1_lsr), .LDB(decoder_1_ldb));
  or or_1 (or_1_out, Ep, and_3_out, and_5_out, and_1_out);
  not not_1 (nLM, or_1_out);
  or or_2 (or_2_out, Cp, and_2_out, and_4_out, and_6_out);
  not not_2 (nCE, or_2_out);
  Ring_Counter ring_counter_1 (
    .T6(ring_counter_1_t6), .T5(ring_counter_1_t5), .T4(ring_counter_1_t4), .T3(ring_counter_1_t3), .T2(Cp),
    .T1(Ep), .CLK(CLK), .CLR(CLR));
  not not_3 (nLi, Cp);
  and and_1 (and_1_out, decoder_1_lda, ring_counter_1_t3);
  or or_3 (or_3_out, and_1_out, and_3_out, and_5_out);
  not not_4 (nEI, or_3_out);
  and and_2 (and_2_out, decoder_1_lda, ring_counter_1_t4);
  or or_4 (or_4_out, 1'b0, and_2_out, ADD);
  not not_5 (nLA, or_4_out);
  not not_6 (nL0, 1'b0);
  and and_3 (and_3_out, decoder_1_ldb, ring_counter_1_t3);
  or or_5 (EU, 1'b0, 1'b0, ADD);
  and and_4 (and_4_out, decoder_1_ldb, ring_counter_1_t4);
  or or_6 (or_6_out, and_6_out, and_4_out, 1'b0);
  not not_7 (nLB, or_6_out);
  and and_5 (and_5_out, decoder_1_add___sub, ring_counter_1_t3);
  and and_6 (and_6_out, decoder_1_add___sub, ring_counter_1_t4);
  and and_7 (ADD, decoder_1_add___sub, ring_counter_1_t5);

  assign EA = 1'b0;
  assign SU = 1'b0;
endmodule

module ADDER (
  input  [7:0] X,
  input  [7:0] Y,
  input  SU,
  output [7:0] S,
  output Cout
);

  wire fa_1_c, fa_2_c, fa_3_c, fa_4_c, fa_5_c, fa_6_c, fa_7_c;
  wire [7:0] bit_extender_1_out, xor_1_out;

  assign xor_1_out = Y ^ bit_extender_1_out;  // XOR_Gate xor_1, 8 bits wide
  assign bit_extender_1_out = {{7{SU}}, SU};  // Bit_Extender bit_extender_1
  FA fa_1 (.X(X[0]), .Y(xor_1_out[0]), .Z(SU), .S(S[0]), .C(fa_1_c));
  FA fa_2 (.X(X[1]), .Y(xor_1_out[1]), .Z(fa_1_c), .S(S[1]), .C(fa_2_c));
  FA fa_3 (.X(X[2]), .Y(xor_1_out[2]), .Z(fa_2_c), .S(S[2]), .C(fa_3_c));
  FA fa_4 (.X(X[3]), .Y(xor_1_out[3]), .Z(fa_3_c), .S(S[3]), .C(fa_4_c));
  FA fa_5 (.X(X[4]), .Y(xor_1_out[4]), .Z(fa_4_c), .S(S[4]), .C(fa_5_c));
  FA fa_6 (.X(X[5]), .Y(xor_1_out[5]), .Z(fa_5_c), .S(S[5]), .C(fa_6_c));
  FA fa_7 (.X(X[6]), .Y(xor_1_out[6]), .Z(fa_6_c), .S(S[6]), .C(fa_7_c));
  FA fa_8 (.X(X[7]), .Y(xor_1_out[7]), .Z(fa_7_c), .S(S[7]), .C(Cout));
endmodule

module INCREMENT (
  input  [7:0] X,
  input  [7:0] Y,
  output [7:0] S,
  output Cout
);

  wire fa_1_c, fa_2_c, fa_3_c, fa_4_c, fa_5_c, fa_6_c, fa_7_c;
  wire [7:0] bit_extender_1_out, xor_1_out;

  assign xor_1_out = Y ^ bit_extender_1_out;  // XOR_Gate xor_1, 8 bits wide
  assign bit_extender_1_out = {{7{1'b0}}, 1'b0};  // Bit_Extender bit_extender_1
  FA fa_1 (.X(X[0]), .Y(xor_1_out[0]), .Z(1'b0), .S(S[0]), .C(fa_1_c));
  FA fa_2 (.X(X[1]), .Y(xor_1_out[1]), .Z(fa_1_c), .S(S[1]), .C(fa_2_c));
  FA fa_3 (.X(X[2]), .Y(xor_1_out[2]), .Z(fa_2_c), .S(S[2]), .C(fa_3_c));
  FA fa_4 (.X(X[3]), .Y(xor_1_out[3]), .Z(fa_3_c), .S(S[3]), .C(fa_4_c));
  FA fa_5 (.X(X[4]), .Y(xor_1_out[4]), .Z(fa_4_c), .S(S[4]), .C(fa_5_c));
  FA fa_6 (.X(X[5]), .Y(xor_1_out[5]), .Z(fa_5_c), .S(S[5]), .C(fa_6_c));
  FA fa_7 (.X(X[6]), .Y(xor_1_out[6]), .Z(fa_6_c), .S(S[6]), .C(fa_7_c));
  FA fa_8 (.X(X[7]), .Y(xor_1_out[7]), .Z(fa_7_c), .S(S[7]), .C(Cout));
endmodule

module DECREMENT (
  input  [7:0] X,
  input  [7:0] Y,
  output [7:0] S,
  output Cout
);

  wire fa_1_c, fa_2_c, fa_3_c, fa_4_c, fa_5_c, fa_6_c, fa_7_c;
  wire [7:0] bit_extender_1_out, xor_1_out;

  assign xor_1_out = Y ^ bit_extender_1_out;  // XOR_Gate xor_1, 8 bits wide
  assign bit_extender_1_out = {{7{1'b1}}, 1'b1};  // Bit_Extender bit_extender_1
  FA fa_1 (.X(X[0]), .Y(xor_1_out[0]), .Z(1'b1), .S(S[0]), .C(fa_1_c));
  FA fa_2 (.X(X[1]), .Y(xor_1_out[1]), .Z(fa_1_c), .S(S[1]), .C(fa_2_c));
  FA fa_3 (.X(X[2]), .Y(xor_1_out[2]), .Z(fa_2_c), .S(S[2]), .C(fa_3_c));
  FA fa_4 (.X(X[3]), .Y(xor_1_out[3]), .Z(fa_3_c), .S(S[3]), .C(fa_4_c));
  FA fa_5 (.X(X[4]), .Y(xor_1_out[4]), .Z(fa_4_c), .S(S[4]), .C(fa_5_c));
  FA fa_6 (.X(X[5]), .Y(xor_1_out[5]), .Z(fa_5_c), .S(S[5]), .C(fa_6_c));
  FA fa_7 (.X(X[6]), .Y(xor_1_out[6]), .Z(fa_6_c), .S(S[6]), .C(fa_7_c));
  FA fa_8 (.X(X[7]), .Y(xor_1_out[7]), .Z(fa_7_c), .S(S[7]), .C(Cout));
endmodule

module COMPARE (
  input  [7:0] ACC,
  input  [7:0] REG_B,
  output EQ,
  output GT,
  output LT
);

  wire not_2_out, not_3_out;
  wire [7:0] adder_1_s, not_1_out;

  ADDER adder_1 (.X(ACC), .Y(REG_B), .SU(1'b1), .S(adder_1_s));  // open: Cout
  assign not_1_out = ~adder_1_s;  // NOT_Gate not_1, 8 bits wide
  and and_1 (EQ, not_1_out[0], not_1_out[1], not_1_out[2], not_1_out[3], not_1_out[4], not_1_out[5], not_1_out[6], not_1_out[7]);
  not not_2 (not_2_out, EQ);
  and and_2 (GT, not_2_out, not_1_out[7]);
  and and_3 (LT, not_2_out, not_3_out);
  not not_3 (not_3_out, GT);
endmodule

module LOGIC_BITWISE_NOT (
  input  [7:0] IN,
  output [7:0] OUT
);

  not not_1 (OUT[0], IN[0]);
  not not_2 (OUT[1], IN[1]);
  not not_3 (OUT[2], IN[2]);
  not not_4 (OUT[3], IN[3]);
  not not_5 (OUT[4], IN[4]);
  not not_6 (OUT[5], IN[5]);
  not not_7 (OUT[6], IN[6]);
  not not_8 (OUT[7], IN[7]);
endmodule

module LOGIC_BITWISE_AND (
  input  [7:0] X,
  input  [7:0] Y,
  output [7:0] OUT
);

  and and_1 (OUT[0], X[0], Y[0]);
  and and_2 (OUT[1], X[1], Y[1]);
  and and_3 (OUT[2], X[2], Y[2]);
  and and_4 (OUT[3], X[3], Y[3]);
  and and_5 (OUT[4], X[4], Y[4]);
  and and_6 (OUT[5], X[5], Y[5]);
  and and_7 (OUT[6], X[6], Y[6]);
  and and_8 (OUT[7], X[7], Y[7]);
endmodule

module LOGIC_BITWISE_OR (
  input  [7:0] X,
  input  [7:0] Y,
  output [7:0] OUT
);

  or or_1 (OUT[0], X[0], Y[0]);
  or or_2 (OUT[1], X[1], Y[1]);
  or or_3 (OUT[2], X[2], Y[2]);
  or or_4 (OUT[3], X[3], Y[3]);
  or or_5 (OUT[4], X[4], Y[4]);
  or or_6 (OUT[5], X[5], Y[5]);
  or or_7 (OUT[6], X[6], Y[6]);
  or or_8 (OUT[7], X[7], Y[7]);
endmodule

module LEFT_SHIFT (
  input  FILL,
  input  [7:0] IN,
  output [7:0] OUT
);


  assign OUT = {IN[6:0], FILL};
endmodule

module RIGHT_SHIFT (
  input  [7:0] IN,
  input  FILL,
  output [7:0] OUT
);


  assign OUT = {FILL, IN[7:1]};
endmodule
